// Digital circuit Alu.dig as structural Verilog
// Arithmetic logic unit module. Supports addition and subtraction.
module Alu (
  input  [7:0] A,
  input  [7:0] B,
  input  SUBTRACT,
  input  nOUT_BUS,
  output [7:0] BUS,
  output [7:0] PEEK
);

  wire _74245_1_pin2, _74245_1_pin3, _74245_1_pin4, _74245_1_pin5, _74245_1_pin6, _74245_1_pin7,
       _74245_1_pin8, _74245_1_pin9, B0xor, B1xor, B2xor, B3xor, B4xor, B5xor, B6xor, B7xor, LOW_C_OUT;

  _74245 _74245_1 (
    .pin1(1'b0), .pin2(_74245_1_pin2), .pin3(_74245_1_pin3), .pin4(_74245_1_pin4), .pin5(_74245_1_pin5),
    .pin6(_74245_1_pin6), .pin7(_74245_1_pin7), .pin8(_74245_1_pin8), .pin9(_74245_1_pin9), .pin10(1'b0),
    .pin11(PEEK[7]), .pin12(PEEK[6]), .pin13(PEEK[5]), .pin14(PEEK[4]), .pin15(PEEK[3]), .pin16(PEEK[2]),
    .pin17(PEEK[1]), .pin18(PEEK[0]), .pin19(nOUT_BUS), .pin20(1'b1));
  BusSplitter #(.Bits(8)) bussplitter_1 (
    .D(BUS), .OE(nOUT_BUS), .D0(_74245_1_pin2), .D1(_74245_1_pin3), .D2(_74245_1_pin4), .D3(_74245_1_pin5),
    .D4(_74245_1_pin6), .D5(_74245_1_pin7), .D6(_74245_1_pin8), .D7(_74245_1_pin9));
  _74283 _74283_1 (
    .pin1(PEEK[5]), .pin2(B5xor), .pin3(A[5]), .pin4(PEEK[4]), .pin5(A[4]), .pin6(B4xor), .pin7(LOW_C_OUT),
    .pin8(1'b0), .pin10(PEEK[7]), .pin11(B7xor), .pin12(A[7]), .pin13(PEEK[6]), .pin14(A[6]), .pin15(B6xor),
    .pin16(1'b1));  // open: pin9
  _74283 _74283_2 (
    .pin1(PEEK[1]), .pin2(B1xor), .pin3(A[1]), .pin4(PEEK[0]), .pin5(A[0]), .pin6(B0xor), .pin7(SUBTRACT),
    .pin8(1'b0), .pin9(LOW_C_OUT), .pin10(PEEK[3]), .pin11(B3xor), .pin12(A[3]), .pin13(PEEK[2]),
    .pin14(A[2]), .pin15(B2xor), .pin16(1'b1));
  _7486 _7486_1 (
    .pin1(B[4]), .pin2(SUBTRACT), .pin3(B4xor), .pin4(B[5]), .pin5(SUBTRACT), .pin6(B5xor), .pin7(1'b0),
    .pin8(B6xor), .pin9(B[6]), .pin10(SUBTRACT), .pin11(B7xor), .pin12(B[7]), .pin13(SUBTRACT), .pin14(1'b1));
  _7486 _7486_2 (
    .pin1(B[0]), .pin2(SUBTRACT), .pin3(B0xor), .pin4(B[1]), .pin5(SUBTRACT), .pin6(B1xor), .pin7(1'b0),
    .pin8(B2xor), .pin9(B[2]), .pin10(SUBTRACT), .pin11(B3xor), .pin12(B[3]), .pin13(SUBTRACT), .pin14(1'b1));

  // Other names for the same wires on the sheet: S0 = PEEK[0]; S1 = PEEK[1]; S2 = PEEK[2]; S3 = PEEK[3]; S4 = PEEK[4];
  //   S5 = PEEK[5]; S6 = PEEK[6]; S7 = PEEK[7]

  // Notes on the sheet:
  //   nOUT_BUS: default 1
  //   B to A (LOW)
  //   Digital workaround for bus sharing
endmodule
