// Digital circuit Mar.dig as structural Verilog
// Memory address register module.
module Mar (
  input  CLOCK,
  input  [7:0] BUS,
  input  nIN_BUS,
  output [7:0] OUTPUT
);

  _74377 _74377_1 (
    .pin1(nIN_BUS), .pin2(OUTPUT[0]), .pin3(BUS[0]), .pin4(BUS[1]), .pin5(OUTPUT[1]), .pin6(OUTPUT[2]),
    .pin7(BUS[2]), .pin8(BUS[3]), .pin9(OUTPUT[3]), .pin10(1'b0), .pin11(CLOCK), .pin12(OUTPUT[4]),
    .pin13(BUS[4]), .pin14(BUS[5]), .pin15(OUTPUT[5]), .pin16(OUTPUT[6]), .pin17(BUS[6]), .pin18(BUS[7]),
    .pin19(OUTPUT[7]), .pin20(1'b1));

  // Other names for the same wires on the sheet: D0 = BUS[0]; D1 = BUS[1]; D2 = BUS[2]; D3 = BUS[3]; D4 = BUS[4];
  //   D5 = BUS[5]; D6 = BUS[6]; D7 = BUS[7]; MAR_IN = nIN_BUS; Q0 = OUTPUT[0]; Q1 = OUTPUT[1]; Q2 = OUTPUT[2];
  //   Q3 = OUTPUT[3]; Q4 = OUTPUT[4]; Q5 = OUTPUT[5]; Q6 = OUTPUT[6]; Q7 = OUTPUT[7]

  // Notes on the sheet:
  //   nIN_BUS: default 1
endmodule
