// Digital circuit Out.dig as structural Verilog
// Out register module.
module Out (
  input  CLOCK,
  input  REFRESH,
  input  [7:0] BUS,
  input  SIGNED_IN,
  input  BUS_nIN,
  output [3:0] PLACE,
  output [6:0] OUT_7SEG
);

  wire _1s, _10s, _100s, and_1_out, dp, OUT_SIGNED, PLACE_Q0, PLACE_Q1, Q0, Q1, Q2, Q3, Q4, Q5, Q6, Q7, SIGN;

  _74377 _74377_1 (
    .pin1(BUS_nIN), .pin2(Q0), .pin3(BUS[0]), .pin4(BUS[1]), .pin5(Q1), .pin6(Q2), .pin7(BUS[2]),
    .pin8(BUS[3]), .pin9(Q3), .pin10(1'b0), .pin11(CLOCK), .pin12(Q4), .pin13(BUS[4]), .pin14(BUS[5]),
    .pin15(Q5), .pin16(Q6), .pin17(BUS[6]), .pin18(BUS[7]), .pin19(Q7), .pin20(1'b1));
  and and_1 (and_1_out, SIGNED_IN, CLOCK);
  EEPROM #(.AddrBits(11), .Bits(8)) eeprom_1 (
    .A({OUT_SIGNED, PLACE_Q1, PLACE_Q0, Q7, Q6, Q5, Q4, Q3, Q2, Q1, Q0}), .CS(~1'b0), .WE(~1'b1), .OE(~1'b0),
    .D({OUT_7SEG, dp}));
  D_FF d_ff_1 (.D(BUS[0]), .C(and_1_out), .Q(OUT_SIGNED));  // open: nQ
  _74161 _74161_1 (
    .pin1(1'b1), .pin2(REFRESH), .pin3(1'b0), .pin4(1'b0), .pin5(1'b0), .pin6(1'b0), .pin7(1'b1),
    .pin8(1'b0), .pin9(1'b1), .pin10(1'b1), .pin13(PLACE_Q1), .pin14(PLACE_Q0), .pin16(1'b1));  // open: pin11, pin12, pin15
  assign PLACE[3] = ~SIGN ? 1'b0 : 1'bz;  // DriverInvSel driverinvsel_1
  assign PLACE[2] = ~_100s ? 1'b0 : 1'bz;  // DriverInvSel driverinvsel_2
  assign PLACE[1] = ~_10s ? 1'b0 : 1'bz;  // DriverInvSel driverinvsel_3
  _74139 _74139_1 (
    .pin1(1'b1), .pin2(1'b0), .pin3(1'b0), .pin8(1'b0), .pin9(SIGN), .pin10(_100s), .pin11(_10s),
    .pin12(_1s), .pin13(PLACE_Q1), .pin14(PLACE_Q0), .pin15(1'b0), .pin16(1'b1));  // open: pin4, pin5, pin6, pin7
  assign PLACE[0] = ~_1s ? 1'b0 : 1'bz;  // DriverInvSel driverinvsel_4

  // Other names for the same wires on the sheet: g = OUT_7SEG[0]; f = OUT_7SEG[1]; e = OUT_7SEG[2]; d = OUT_7SEG[3];
  //   c = OUT_7SEG[4]; b = OUT_7SEG[5]; a = OUT_7SEG[6]; _1s_t = PLACE[0]; _10s_t = PLACE[1]; _100s_t = PLACE[2];
  //   D0 = BUS[0]; D1 = BUS[1]; D2 = BUS[2]; D3 = BUS[3]; D4 = BUS[4]; D5 = BUS[5]; D6 = BUS[6]; D7 = BUS[7];
  //   SIGN_t = PLACE[3]

  // Notes on the sheet:
  //   REFRESH: Hz: 20
  //   OUT_7SEG: a (6) bcdef g (0)
  //   contents of eeprom_1 (hex, n*v repeats v):
  //   fc,60,da,f2,66,b6,be,e0,fe,f6,fc,60,da,f2,66,b6,be,e0,fe,f6,fc,60,da,f2,66,b6,be,
  //   e0,fe,f6,fc,60,da,f2,66,b6,be,e0,fe,f6,fc,60,da,f2,66,b6,be,e0,fe,f6,fc,60,da,f2,
  //   66,b6,be,e0,fe,f6,fc,60,da,f2,66,b6,be,e0,fe,f6,fc,60,da,f2,66,b6,be,e0,fe,f6,fc,
  //   60,da,f2,66,b6,be,e0,fe,f6,fc,60,da,f2,66,b6,be,e0,fe,f6,fc,60,da,f2,66,b6,be,e0,
  //   fe,f6,fc,60,da,f2,66,b6,be,e0,fe,f6,fc,60,da,f2,66,b6,be,e0,fe,f6,fc,60,da,f2,66,
  //   b6,be,e0,fe,f6,fc,60,da,f2,66,b6,be,e0,fe,f6,fc,60,da,f2,66,b6,be,e0,fe,f6,fc,60,
  //   da,f2,66,b6,be,e0,fe,f6,fc,60,da,f2,66,b6,be,e0,fe,f6,fc,60,da,f2,66,b6,be,e0,fe,
  //   f6,fc,60,da,f2,66,b6,be,e0,fe,f6,fc,60,da,f2,66,b6,be,e0,fe,f6,fc,60,da,f2,66,b6,
  //   be,e0,fe,f6,fc,60,da,f2,66,b6,be,e0,fe,f6,fc,60,da,f2,66,b6,be,e0,fe,f6,fc,60,da,
  //   f2,66,b6,be,e0,fe,f6,fc,60,da,f2,66,b6,fc,fc,fc,fc,fc,fc,fc,fc,fc,fc,60,60,60,60,
  //   60,60,60,60,60,60,da,da,da,da,da,da,da,da,da,da,f2,f2,f2,f2,f2,f2,f2,f2,f2,f2,66,
  //   66,66,66,66,66,66,66,66,66,b6,b6,b6,b6,b6,b6,b6,b6,b6,b6,be,be,be,be,be,be,be,be,
  //   be,be,e0,e0,e0,e0,e0,e0,e0,e0,e0,e0,fe,fe,fe,fe,fe,fe,fe,fe,fe,fe,f6,f6,f6,f6,f6,
  //   f6,f6,f6,f6,f6,fc,fc,fc,fc,fc,fc,fc,fc,fc,fc,60,60,60,60,60,60,60,60,60,60,da,da,
  //   da,da,da,da,da,da,da,da,f2,f2,f2,f2,f2,f2,f2,f2,f2,f2,66,66,66,66,66,66,66,66,66,
  //   66,b6,b6,b6,b6,b6,b6,b6,b6,b6,b6,be,be,be,be,be,be,be,be,be,be,e0,e0,e0,e0,e0,e0,
  //   e0,e0,e0,e0,fe,fe,fe,fe,fe,fe,fe,fe,fe,fe,f6,f6,f6,f6,f6,f6,f6,f6,f6,f6,fc,fc,fc,
  //   fc,fc,fc,fc,fc,fc,fc,60,60,60,60,60,60,60,60,60,60,da,da,da,da,da,da,da,da,da,da,
  //   f2,f2,f2,f2,f2,f2,f2,f2,f2,f2,66,66,66,66,66,66,66,66,66,66,b6,b6,b6,b6,b6,b6,fc,
  //   fc,fc,fc,fc,fc,fc,fc,fc,fc,fc,fc,fc,fc,fc,fc,fc,fc,fc,fc,fc,fc,fc,fc,fc,fc,fc,fc,
  //   fc,fc,fc,fc,fc,fc,fc,fc,fc,fc,fc,fc,fc,fc,fc,fc,fc,fc,fc,fc,fc,fc,fc,fc,fc,fc,fc,
  //   fc,fc,fc,fc,fc,fc,fc,fc,fc,fc,fc,fc,fc,fc,fc,fc,fc,fc,fc,fc,fc,fc,fc,fc,fc,fc,fc,
  //   fc,fc,fc,fc,fc,fc,fc,fc,fc,fc,fc,fc,fc,fc,fc,fc,fc,fc,60,60,60,60,60,60,60,60,60,
  //   60,60,60,60,60,60,60,60,60,60,60,60,60,60,60,60,60,60,60,60,60,60,60,60,60,60,60,
  //   60,60,60,60,60,60,60,60,60,60,60,60,60,60,60,60,60,60,60,60,60,60,60,60,60,60,60,
  //   60,60,60,60,60,60,60,60,60,60,60,60,60,60,60,60,60,60,60,60,60,60,60,60,60,60,60,
  //   60,60,60,60,60,60,60,60,60,60,da,da,da,da,da,da,da,da,da,da,da,da,da,da,da,da,da,
  //   da,da,da,da,da,da,da,da,da,da,da,da,da,da,da,da,da,da,da,da,da,da,da,da,da,da,da,
  //   da,da,da,da,da,da,da,da,da,da,da,da,0,0,0,0,0,0,0,0,0,0,0,0,0,0,0,0,0,0,0,0,0,0,0,
  //   0,0,0,0,0,0,0,0,0,0,0,0,0,0,0,0,0,0,0,0,0,0,0,0,0,0,0,0,0,0,0,0,0,0,0,0,0,0,0,0,0,
  //   0,0,0,0,0,0,0,0,0,0,0,0,0,0,0,0,0,0,0,0,0,0,0,0,0,0,0,0,0,0,0,0,0,0,0,0,0,0,0,0,0,
  //   0,0,0,0,0,0,0,0,0,0,0,0,0,0,0,0,0,0,0,0,0,0,0,0,0,0,0,0,0,0,0,0,0,0,0,0,0,0,0,0,0,
  //   0,0,0,0,0,0,0,0,0,0,0,0,0,0,0,0,0,0,0,0,0,0,0,0,0,0,0,0,0,0,0,0,0,0,0,0,0,0,0,0,0,
  //   0,0,0,0,0,0,0,0,0,0,0,0,0,0,0,0,0,0,0,0,0,0,0,0,0,0,0,0,0,0,0,0,0,0,0,0,0,0,0,0,0,
  //   0,0,0,0,0,0,0,0,0,0,0,0,0,0,0,0,0,0,0,0,0,0,0,0,0,0,0,0,fc,60,da,f2,66,b6,be,e0,fe,
  //   f6,fc,60,da,f2,66,b6,be,e0,fe,f6,fc,60,da,f2,66,b6,be,e0,fe,f6,fc,60,da,f2,66,b6,
  //   be,e0,fe,f6,fc,60,da,f2,66,b6,be,e0,fe,f6,fc,60,da,f2,66,b6,be,e0,fe,f6,fc,60,da,
  //   f2,66,b6,be,e0,fe,f6,fc,60,da,f2,66,b6,be,e0,fe,f6,fc,60,da,f2,66,b6,be,e0,fe,f6,
  //   fc,60,da,f2,66,b6,be,e0,fe,f6,fc,60,da,f2,66,b6,be,e0,fe,f6,fc,60,da,f2,66,b6,be,
  //   e0,fe,f6,fc,60,da,f2,66,b6,be,e0,fe,e0,be,b6,66,f2,da,60,fc,f6,fe,e0,be,b6,66,f2,
  //   da,60,fc,f6,fe,e0,be,b6,66,f2,da,60,fc,f6,fe,e0,be,b6,66,f2,da,60,fc,f6,fe,e0,be,
  //   b6,66,f2,da,60,fc,f6,fe,e0,be,b6,66,f2,da,60,fc,f6,fe,e0,be,b6,66,f2,da,60,fc,f6,
  //   fe,e0,be,b6,66,f2,da,60,fc,f6,fe,e0,be,b6,66,f2,da,60,fc,f6,fe,e0,be,b6,66,f2,da,
  //   60,fc,f6,fe,e0,be,b6,66,f2,da,60,fc,f6,fe,e0,be,b6,66,f2,da,60,fc,f6,fe,e0,be,b6,
  //   66,f2,da,60,fc,fc,fc,fc,fc,fc,fc,fc,fc,fc,60,60,60,60,60,60,60,60,60,60,da,da,da,
  //   da,da,da,da,da,da,da,f2,f2,f2,f2,f2,f2,f2,f2,f2,f2,66,66,66,66,66,66,66,66,66,66,
  //   b6,b6,b6,b6,b6,b6,b6,b6,b6,b6,be,be,be,be,be,be,be,be,be,be,e0,e0,e0,e0,e0,e0,e0,
  //   e0,e0,e0,fe,fe,fe,fe,fe,fe,fe,fe,fe,fe,f6,f6,f6,f6,f6,f6,f6,f6,f6,f6,fc,fc,fc,fc,
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  //   Digital workaround. Use z for faking led refresh rate.
endmodule
