// Digital circuit Processor.dig as structural Verilog
module Processor (
  input  CLOCK,
  input  REFRESH
);

  wire _1s, _10s, _100s, a, ALU_BUS_nOUT, ALU_BUS_OUT, ALU_SUBTRACT, b, c, comparator_1_gt, d, e, f, g, HALT,
       IR_BUS_IN, IR_BUS_nIN, IR_BUS_nOUT, IR_BUS_OUT, jk_ff_1_q, MAR_BUS_IN, MAR_BUS_nIN, nCLOCK, not_2_out,
       nRESET, OUT_BUS_IN, OUT_BUS_nIN, OUT_SIGNED_IN, PC_BUS_IN, PC_BUS_nIN, PC_BUS_nOUT, PC_BUS_OUT,
       PC_COUNT, PEEK_INSTRUCTION, PEEK_STEP, RAM_BUS_IN, RAM_BUS_nIN, RAM_BUS_nOUT, RAM_BUS_OUT,
       REGA_BUS_IN, REGA_BUS_nIN, REGA_BUS_nOUT, REGA_BUS_OUT, REGB_BUS_IN, REGB_BUS_nIN, REGB_BUS_nOUT,
       REGB_BUS_OUT, RESET, reset_1_out, SIGN, ZERO_BUS_nOUT, ZERO_BUS_OUT;
  wire [2:0] counter_1_out, PEEK_BUS_IN_ADDRESS, PEEK_CONTROL, PEEK_LAST_STEP;
  wire [3:0] PEEK_BUS_OUT_ADDRESS;
  wire [6:6] out_1_out_7seg;
  wire [7:0] BUS, OUT_IR, OUT_MAR, OUT_REG_A, OUT_REG_B, PEEK_ALU, PEEK_PC, PEEK_RAM;

  JK_FF jk_ff_1 (.J(HALT), .C(CLOCK), .K(1'b0), .Q(jk_ff_1_q));  // open: nQ
  Stop u_HALT (.stop(jk_ff_1_q));
  Pc pc_1 (
    .CLOCK(CLOCK), .nRESET(nRESET), .COUNT(PC_COUNT), .BUS_nIN(PC_BUS_nIN), .BUS_nOUT(PC_BUS_nOUT),
    .BUS(BUS), .PEEK(PEEK_PC));
  Ram ram_1 (
    .CLOCK(CLOCK), .ADDRESS(OUT_MAR), .BUS_nIN(RAM_BUS_nIN), .BUS_nOUT(RAM_BUS_nOUT), .BUS(BUS),
    .PEEK(PEEK_RAM));
  Mar mar_1 (.CLOCK(CLOCK), .RESET(RESET), .BUS(BUS), .BUS_nIN(MAR_BUS_nIN), .OUT(OUT_MAR));
  Register u_A (.CLOCK(CLOCK), .nIN_BUS(REGA_BUS_nIN), .nOUT_BUS(REGA_BUS_nOUT), .BUS(BUS), .OUTPUT(OUT_REG_A));
  Register u_B (.CLOCK(CLOCK), .nIN_BUS(REGB_BUS_nIN), .nOUT_BUS(REGB_BUS_nOUT), .BUS(BUS), .OUTPUT(OUT_REG_B));
  Alu alu_1 (
    .A(OUT_REG_A), .B(OUT_REG_B), .SUBTRACT(ALU_SUBTRACT), .nOUT_BUS(ALU_BUS_nOUT), .BUS(BUS), .PEEK(PEEK_ALU));
  Out out_1 (
    .CLOCK(CLOCK), .REFRESH(REFRESH), .BUS(BUS), .SIGNED_IN(OUT_SIGNED_IN), .BUS_nIN(OUT_BUS_nIN),
    .PLACE({SIGN, _100s, _10s, _1s}), .OUT_7SEG({out_1_out_7seg[6], b, c, d, e, f, g}));
  Ir ir_1 (.CLOCK(nCLOCK), .BUS_nIN(IR_BUS_nIN), .BUS_nOUT(IR_BUS_nOUT), .BUS(BUS), .OUT(OUT_IR));
  Control control_1 (
    .nCLOCK(nCLOCK), .nRESET(nRESET), .IR(OUT_IR), .HALT(HALT), .PC_COUNT(PC_COUNT),
    .ALU_SUBTRACT(ALU_SUBTRACT), .OUT_SIGNED_IN(OUT_SIGNED_IN), .FLAGS_IN(ZERO_BUS_nOUT),
    .ZERO_BUS_nOUT(RAM_BUS_nOUT), .RAM_BUS_nOUT(PC_BUS_nOUT), .PC_BUS_nOUT(IR_BUS_nOUT),
    .IR_BUS_nOUT(REGA_BUS_nOUT), .REGA_BUS_nOUT(REGB_BUS_nOUT), .REGB_BUS_nOUT(ALU_BUS_nOUT),
    .ALU_BUS_nOUT(RAM_BUS_nIN), .RAM_BUS_nIN(MAR_BUS_nIN), .MAR_BUS_nIN(PC_BUS_nIN), .PC_BUS_nIN(IR_BUS_nIN),
    .IR_BUS_nIN(REGA_BUS_nIN), .REGA_BUS_nIN(REGB_BUS_nIN), .REGB_BUS_nIN(OUT_BUS_nIN),
    .OUT_BUS_nIN(PEEK_STEP), .PEEK_STEP(PEEK_LAST_STEP), .PEEK_LAST_STEP(PEEK_INSTRUCTION),
    .PEEK_INSTRUCTION(PEEK_BUS_OUT_ADDRESS), .PEEK_BUS_OUT_ADDRESS(PEEK_BUS_IN_ADDRESS),
    .PEEK_BUS_IN_ADDRESS(PEEK_CONTROL));  // open: FLAGS, PEEK_CONTROL
  not not_1 (nCLOCK, CLOCK);
  // Probe ~CLOCK on nCLOCK
  LED led_1 (.in(BUS[7]));
  LED led_2 (.in(PEEK_PC[7]));
  LED led_3 (.in(PEEK_RAM[7]));
  LED led_4 (.in(OUT_MAR[7]));
  LED led_5 (.in(OUT_IR[7]));
  LED led_6 (.in(OUT_REG_A[7]));
  LED led_7 (.in(OUT_REG_B[7]));
  LED led_8 (.in(PEEK_ALU[7]));
  LED led_9 (.in(BUS[3]));
  LED led_10 (.in(BUS[4]));
  LED led_11 (.in(BUS[5]));
  LED led_12 (.in(BUS[6]));
  LED led_13 (.in(PEEK_PC[3]));
  LED led_14 (.in(PEEK_PC[4]));
  LED led_15 (.in(PEEK_PC[5]));
  LED led_16 (.in(PEEK_PC[6]));
  LED led_17 (.in(PEEK_RAM[3]));
  LED led_18 (.in(PEEK_RAM[4]));
  LED led_19 (.in(PEEK_RAM[5]));
  LED led_20 (.in(PEEK_RAM[6]));
  LED led_21 (.in(OUT_MAR[3]));
  LED led_22 (.in(OUT_MAR[4]));
  LED led_23 (.in(OUT_MAR[5]));
  LED led_24 (.in(OUT_MAR[6]));
  LED led_25 (.in(OUT_IR[3]));
  LED led_26 (.in(OUT_IR[4]));
  LED led_27 (.in(OUT_IR[5]));
  LED led_28 (.in(OUT_IR[6]));
  LED led_29 (.in(OUT_REG_A[3]));
  LED led_30 (.in(OUT_REG_A[4]));
  LED led_31 (.in(OUT_REG_A[5]));
  LED led_32 (.in(OUT_REG_A[6]));
  LED led_33 (.in(OUT_REG_B[3]));
  LED led_34 (.in(OUT_REG_B[4]));
  LED led_35 (.in(OUT_REG_B[5]));
  LED led_36 (.in(OUT_REG_B[6]));
  LED led_37 (.in(PEEK_ALU[3]));
  LED led_38 (.in(PEEK_ALU[4]));
  LED led_39 (.in(PEEK_ALU[5]));
  LED led_40 (.in(PEEK_ALU[6]));
  LED led_41 (.in(BUS[0]));
  LED led_42 (.in(BUS[1]));
  LED led_43 (.in(BUS[2]));
  LED led_44 (.in(PEEK_PC[0]));
  LED led_45 (.in(PEEK_PC[1]));
  LED led_46 (.in(PEEK_PC[2]));
  LED led_47 (.in(PEEK_RAM[0]));
  LED led_48 (.in(PEEK_RAM[1]));
  LED led_49 (.in(PEEK_RAM[2]));
  LED led_50 (.in(OUT_MAR[0]));
  LED led_51 (.in(OUT_MAR[1]));
  LED led_52 (.in(OUT_MAR[2]));
  LED led_53 (.in(OUT_IR[0]));
  LED led_54 (.in(OUT_IR[1]));
  LED led_55 (.in(OUT_IR[2]));
  LED led_56 (.in(OUT_REG_A[0]));
  LED led_57 (.in(OUT_REG_A[1]));
  LED led_58 (.in(OUT_REG_A[2]));
  LED led_59 (.in(OUT_REG_B[0]));
  LED led_60 (.in(OUT_REG_B[1]));
  LED led_61 (.in(OUT_REG_B[2]));
  LED led_62 (.in(PEEK_ALU[0]));
  LED led_63 (.in(PEEK_ALU[1]));
  LED led_64 (.in(PEEK_ALU[2]));
  assign BUS = ~ZERO_BUS_nOUT ? {8{1'b0}} : 8'bz;  // DriverInvSel driverinvsel_1
  LED led_65 (.in(HALT));
  LED led_66 (.in(PC_COUNT));
  LED led_67 (.in(ALU_SUBTRACT));
  LED led_68 (.in(OUT_SIGNED_IN));
  LED led_69 (.in(ZERO_BUS_OUT));
  LED led_70 (.in(RAM_BUS_OUT));
  LED led_71 (.in(PC_BUS_OUT));
  LED led_72 (.in(IR_BUS_OUT));
  LED led_73 (.in(REGA_BUS_OUT));
  LED led_74 (.in(REGB_BUS_OUT));
  LED led_75 (.in(ALU_BUS_OUT));
  LED led_76 (.in(RAM_BUS_IN));
  LED led_77 (.in(MAR_BUS_IN));
  LED led_78 (.in(PC_BUS_IN));
  LED led_79 (.in(IR_BUS_IN));
  LED led_80 (.in(REGA_BUS_IN));
  LED led_81 (.in(REGB_BUS_IN));
  LED led_82 (.in(OUT_BUS_IN));
  Counter #(.Bits(3)) counter_1 (.en(not_2_out), .C(CLOCK), .clr(reset_1_out), .out(counter_1_out));  // open: ovf
  Reset #(.invertOutput("false")) reset_1 (.out(reset_1_out));
  Seven_Seg #(.commonCathode("true"), .ledPersistence("true")) seven_seg_1 (
    .a(a), .b(b), .c(c), .d(d), .e(e), .f(f), .g(g), .dp(1'b0), .common(SIGN));
  Comparator #(.Bits(3)) comparator_1 (.a(counter_1_out), .b(3'b010), .gt(comparator_1_gt), .lt(RESET));  // open: eq
  Seven_Seg #(.commonCathode("true"), .ledPersistence("true")) seven_seg_2 (
    .a(a), .b(b), .c(c), .d(d), .e(e), .f(f), .g(g), .dp(1'b0), .common(_100s));
  not not_2 (not_2_out, comparator_1_gt);
  Seven_Seg #(.commonCathode("true"), .ledPersistence("true")) seven_seg_3 (
    .a(a), .b(b), .c(c), .d(d), .e(e), .f(f), .g(g), .dp(1'b0), .common(_10s));
  not not_3 (ZERO_BUS_OUT, ZERO_BUS_nOUT);
  not not_4 (RAM_BUS_OUT, RAM_BUS_nOUT);
  not not_5 (PC_BUS_OUT, PC_BUS_nOUT);
  not not_6 (IR_BUS_OUT, IR_BUS_nOUT);
  not not_7 (REGA_BUS_OUT, REGA_BUS_nOUT);
  not not_8 (REGB_BUS_OUT, REGB_BUS_nOUT);
  not not_9 (ALU_BUS_OUT, ALU_BUS_nOUT);
  not not_10 (RAM_BUS_IN, RAM_BUS_nIN);
  not not_11 (MAR_BUS_IN, MAR_BUS_nIN);
  not not_12 (PC_BUS_IN, PC_BUS_nIN);
  not not_13 (IR_BUS_IN, IR_BUS_nIN);
  not not_14 (REGA_BUS_IN, REGA_BUS_nIN);
  not not_15 (REGB_BUS_IN, REGB_BUS_nIN);
  not not_16 (OUT_BUS_IN, OUT_BUS_nIN);
  // Probe on RESET
  // Probe on CLOCK
  // Probe on nCLOCK
  // Probe PC on PEEK_PC
  // Probe MAR on OUT_MAR
  // Probe RAM on PEEK_RAM
  // Probe BUS on BUS
  // Probe STEP on PEEK_STEP
  // Probe LAST STEP on PEEK_LAST_STEP
  // Probe IR on OUT_IR
  // Probe CONTROL on PEEK_CONTROL
  // Probe BUS IN ADDRESS on PEEK_BUS_IN_ADDRESS
  // Probe BUS OUT ADDRESS on PEEK_BUS_OUT_ADDRESS
  // Probe REGA on OUT_REG_A
  // Probe REGB on OUT_REG_B
  // Probe ALU on PEEK_ALU
  not not_17 (nRESET, RESET);
  Seven_Seg #(.commonCathode("true"), .ledPersistence("true")) seven_seg_4 (
    .a(a), .b(b), .c(c), .d(d), .e(e), .f(f), .g(g), .dp(1'b0), .common(_1s));

  // Notes on the sheet:
  //   CLOCK: Hz: 4
  //   REFRESH: Hz: 20
  //   Digital workaround as leds can only be connected from cathode
endmodule
