// Digital circuit Ram.dig as structural Verilog
// RAM module.
module Ram (
  input  CLOCK,
  input  [7:0] ADDRESS,
  input  nIN_BUS,
  input  nOUT_BUS,
  output [7:0] BUS,
  output [7:0] PEEK
);

  wire _74245_1_pin11, _74245_1_pin12, _74245_1_pin13, _74245_1_pin14, _74245_1_pin15, _74245_1_pin16,
       _74245_1_pin17, _74245_1_pin18, _74245_1_pin19, CLOCK_WRITE, IN_BUS, nand_1_out, nand_2_out,
       nand_3_out, not_1_out, not_3_out, not_4_out;

  not not_1 (not_1_out, CLOCK);
  not not_2 (IN_BUS, nIN_BUS);
  not not_3 (not_3_out, not_1_out);
  not not_4 (not_4_out, not_3_out);
  nand nand_1 (nand_1_out, CLOCK, not_4_out);
  _74245 _74245_1 (
    .pin1(nIN_BUS), .pin2(PEEK[7]), .pin3(PEEK[6]), .pin4(PEEK[5]), .pin5(PEEK[4]), .pin6(PEEK[3]),
    .pin7(PEEK[2]), .pin8(PEEK[1]), .pin9(PEEK[0]), .pin10(1'b0), .pin11(_74245_1_pin11),
    .pin12(_74245_1_pin12), .pin13(_74245_1_pin13), .pin14(_74245_1_pin14), .pin15(_74245_1_pin15),
    .pin16(_74245_1_pin16), .pin17(_74245_1_pin17), .pin18(_74245_1_pin18), .pin19(_74245_1_pin19),
    .pin20(1'b1));
  not not_5 (CLOCK_WRITE, nand_1_out);
  nand nand_2 (nand_2_out, nIN_BUS, nOUT_BUS);
  not not_6 (_74245_1_pin19, nand_2_out);
  // Probe CLOCK_WRITE on CLOCK_WRITE
  BusSplitter #(.Bits(8)) bussplitter_1 (
    .D(BUS), .OE(nOUT_BUS), .D0(_74245_1_pin11), .D1(_74245_1_pin12), .D2(_74245_1_pin13),
    .D3(_74245_1_pin14), .D4(_74245_1_pin15), .D5(_74245_1_pin16), .D6(_74245_1_pin17), .D7(_74245_1_pin18));
  nand nand_3 (nand_3_out, CLOCK_WRITE, IN_BUS);
  // Probe ~WE_RAM on nand_3_out
  // A623308A a623308a_1: pin names not known; wires that end beside it: 1'b1, nand_3_out, 1'b0, ADDRESS[7], 1'b0, ADDRESS[6], 1'b0, ADDRESS[5], 1'b0, ADDRESS[4], IN_BUS, ADDRESS[3], 1'b0, ADDRESS[2], 1'b0, ADDRESS[1], PEEK[7], ADDRESS[0], PEEK[0], PEEK[1], PEEK[2], 1'b0

  // Other names for the same wires on the sheet: IN_OUT_D0 = PEEK[0]; IN_OUT_D1 = PEEK[1]; IN_OUT_D2 = PEEK[2];
  //   IN_OUT_D3 = PEEK[3]; IN_OUT_D4 = PEEK[4]; IN_OUT_D5 = PEEK[5]; IN_OUT_D6 = PEEK[6]; IN_OUT_D7 = PEEK[7]

  // Notes on the sheet:
  //   nIN_BUS: default 1
  //   nOUT_BUS: Active low, default 1
  //   Digital workaround for bus sharing
endmodule
